# Fritzing sketch hawe_sht20 (saved by Fritzing 1.0.3b)

parts:
  A1 = Raspberry Pi Pico2
  Part1 = Adafruit AHT20 Temperature and Humidity Sensor [part_number="Adafruit #4566"]

nets:
  N1: A1.pin_1, Part1.SCL
  N2: A1.pin_2, Part1.SDA
  N3: A1.pin_36, Part1.VCC
  N4: A1.pin_39, Part1.GND

custom parts:
  Raspberry Pi Pico2: Raspberry Pi Pico 2 is our new $5 microcontroller board, built on RP2350: our new high-performance, secure microcontroller.
  Adafruit AHT20 Temperature and Humidity Sensor: The AHT20 is a nice but inexpensive temperature and humidity sensor from the same folks that brought us the DHT22. You can take sensor readings as often as you like, and it uses standard I2C so its super easy to use with any Arduino or Linux/Raspberry Pi board. This sensor has a typical accuracy of +- 2% relative humidity, and +-0.3 °C. There is only one I2C address so its not a good option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
